# Fritzing sketch IRVeh_Schema (saved by Fritzing 0.9.2b)
breadboards: 1

parts:
  Part1 = Rotoshield - Motor driver shield for Arduino
  M1 = DC Motor
  M2 = DC Motor
  VCC1 = Battery block 9V
  IR1 = TSOP312.., 314.. [package=THT]
  Part2 = Arduino Uno (Rev3)  # not connected
  Part3 = SRF05 Ultrasonic Rangefinder
  LED1 = smd LED [color="Red (633nm)" package="0805 [SMD]"]
  R1 = Resistor [tolerance=±5% resistance=220 package="1206 [SMD]"]

nets:
  N1: Part1.A_IN_0, Part3.Echo
  N2: Part1.A_IN_1, Part3.Trig
  N3: Part1.A_IN_5, IR1.GND
  N4: Part1.DIG_10, R1.Pin_0
  +5V: Part1.+5V, IR1.Data, Part3.VCC
  GND: Part1.GND, VCC1.-, IR1.Vs, Part3.GND, LED1.anode
  N5: Part1.M3-2, M1.pin_2
  N6: Part1.M3-1, M1.pin_1
  N7: Part1.M4-2, M2.pin_2
  N8: Part1.M4-1, M2.pin_1
  N9: Part1.VCC, VCC1.+
  N10: LED1.cathode, R1.Pin_1
